// Logisim project Basic_Circuits (XOR,Adders).circ as structural Verilog
module Half_Adder (
  input  A,
  input  B,
  output Sum,
  output Carry
);

  xor xor_1 (Sum, A, B);
  and and_1 (Carry, A, B);
endmodule

module Full_adder (
  input  in_1,
  input  in_2,
  input  in_3,
  input  A,
  input  B,
  input  C_in,
  output out_7,
  output Interim_sum,
  output C_out,
  output Final_Sum
);

  wire and_1_out, and_2_out, half_adder_1_carry, half_adder_2_carry, xor_1_out, xor_2_out;

  xor xor_1 (xor_1_out, in_1, in_2);
  and and_1 (and_1_out, in_1, in_2);
  xor xor_2 (xor_2_out, in_3, xor_1_out);
  and and_2 (and_2_out, in_3, xor_1_out);
  Half_Adder half_adder_1 (.A(A), .B(B), .Sum(Interim_sum), .Carry(half_adder_1_carry));
  Half_Adder half_adder_2 (.A(Interim_sum), .B(C_in), .Sum(Final_Sum), .Carry(half_adder_2_carry));
  LED led_1 (.in(Final_Sum));
  or or_1 (out_7, and_1_out, and_2_out);
  or or_2 (C_out, half_adder_1_carry, half_adder_2_carry);
  LED led_2 (.in(C_out));
endmodule

module XOR_Gate (
  input  A,
  input  B,
  output Ans
);

  wire and_1_out, not_1_out, not_2_out, or_1_out, or_2_out, or_3_out;

  or or_1 (or_1_out, A, B);
  not not_1 (not_1_out, A);
  not not_2 (not_2_out, B);
  and and_1 (and_1_out, A, B);
  or or_2 (or_2_out, not_1_out, not_2_out);
  or or_3 (or_3_out, and_1_out, or_1_out);
  and and_2 (Ans, or_3_out, or_2_out);

  // Notes on the sheet:
  //   XOR gate = [ (A AND B) OR (A OR B) ] AND (NOT A OR NOT B)
endmodule

module Full_adder_simple (
  input  in_1,
  input  in_2,
  input  in_3,
  output out_4,
  output out_5
);

  wire and_1_out, and_2_out, xor_1_out;

  xor xor_1 (xor_1_out, in_1, in_2);
  and and_1 (and_1_out, in_1, in_2);
  xor xor_2 (out_5, in_3, xor_1_out);
  and and_2 (and_2_out, in_3, xor_1_out);
  or or_1 (out_4, and_1_out, and_2_out);
endmodule

module Xor_Gate_For_Three (
  input  A,
  input  B,
  input  C,
  output Interim_Ans,
  output Ans
);

  XOR_Gate xor_gate_1 (.A(A), .B(B), .Ans(Interim_Ans));
  XOR_Gate xor_gate_2 (.A(Interim_Ans), .B(C), .Ans(Ans));
endmodule

module Two_Bit_Adder (
  input  [1:0] Two
);
endmodule
